// Digital circuit CC.dig as structural Verilog
module CC (
  input  [6:0] OPCD,
  input  [2:0] F3,
  output IMM,
  output BRG,
  output STR,
  output LD,
  output [1:0] PC,
  output [1:0] DADO
);

  wire and_1_out, and_2_out, and_3_out, and_4_out, and_5_out, and_6_out, and_7_out, and_8_out, and_9_out,
       and_10_out, and_11_out, and_12_out, and_13_out, and_14_out, and_15_out, and_16_out, and_17_out,
       and_18_out, and_19_out, and_20_out, and_21_out, and_22_out, and_23_out, and_24_out, and_25_out,
       and_26_out, and_27_out, and_28_out, not_1_out, not_2_out, not_3_out, not_4_out, not_5_out, not_6_out,
       not_7_out, not_8_out, not_9_out, not_10_out, not_11_out, not_12_out, not_13_out, not_14_out,
       not_15_out, not_16_out, not_17_out, not_18_out, not_19_out, not_20_out, not_21_out, not_22_out;
  wire [2:0] or_1_out;

  ROM #(.AddrBits(3), .Bits(7)) rom_1 (.A(or_1_out), .sel(1'b1), .D({DADO[0], PC, LD, STR, BRG, IMM}));
  not not_1 (not_1_out, OPCD[6]);
  and and_1 (and_1_out, OPCD[5], not_1_out);
  or or_1 (or_1_out[0], and_27_out, and_19_out, and_11_out, and_3_out);
  or or_2 (or_1_out[1], and_27_out, and_23_out, and_11_out, and_7_out);
  or or_3 (or_1_out[2], and_27_out, and_23_out, and_19_out, and_15_out);
  not not_2 (not_2_out, OPCD[3]);
  not not_3 (not_3_out, OPCD[2]);
  and and_2 (and_2_out, not_2_out, OPCD[4]);
  and and_3 (and_3_out, and_4_out, and_2_out, and_1_out);
  not not_4 (not_4_out, OPCD[6]);
  and and_4 (and_4_out, OPCD[0], OPCD[1], not_3_out);
  not not_5 (not_5_out, OPCD[5]);
  and and_5 (and_5_out, not_5_out, not_4_out);
  not not_6 (not_6_out, OPCD[3]);
  not not_7 (not_7_out, OPCD[2]);
  and and_6 (and_6_out, not_6_out, OPCD[4]);
  and and_7 (and_7_out, and_8_out, and_6_out, and_5_out);
  and and_8 (and_8_out, OPCD[0], OPCD[1], not_7_out);
  not not_8 (not_8_out, OPCD[6]);
  not not_9 (not_9_out, OPCD[5]);
  and and_9 (and_9_out, not_9_out, not_8_out);
  not not_10 (not_10_out, OPCD[4]);
  not not_11 (not_11_out, OPCD[3]);
  and and_10 (and_10_out, not_11_out, not_10_out);
  and and_11 (and_11_out, and_12_out, and_10_out, and_9_out);
  not not_12 (not_12_out, OPCD[2]);
  and and_12 (and_12_out, OPCD[0], OPCD[1], not_12_out);
  not not_13 (not_13_out, OPCD[6]);
  and and_13 (and_13_out, OPCD[5], not_13_out);
  not not_14 (not_14_out, OPCD[4]);
  not not_15 (not_15_out, OPCD[3]);
  and and_14 (and_14_out, not_15_out, not_14_out);
  and and_15 (and_15_out, and_16_out, and_14_out, and_13_out);
  not not_16 (not_16_out, OPCD[2]);
  and and_16 (and_16_out, OPCD[0], OPCD[1], not_16_out);
  not not_17 (not_17_out, OPCD[4]);
  and and_17 (and_17_out, OPCD[5], OPCD[6]);
  not not_18 (not_18_out, OPCD[3]);
  not not_19 (not_19_out, OPCD[2]);
  and and_18 (and_18_out, not_18_out, not_17_out);
  and and_19 (and_19_out, and_20_out, and_18_out, and_17_out);
  and and_20 (and_20_out, OPCD[0], OPCD[1], not_19_out);
  not not_20 (not_20_out, OPCD[4]);
  and and_21 (and_21_out, OPCD[5], OPCD[6]);
  and and_22 (and_22_out, OPCD[3], not_20_out);
  and and_23 (and_23_out, and_24_out, and_22_out, and_21_out);
  and and_24 (and_24_out, OPCD[0], OPCD[1], OPCD[2]);
  and and_25 (and_25_out, OPCD[5], OPCD[6]);
  not not_21 (not_21_out, OPCD[4]);
  not not_22 (not_22_out, OPCD[3]);
  and and_26 (and_26_out, not_22_out, not_21_out);
  and and_27 (and_27_out, and_28_out, and_26_out, and_25_out);
  and and_28 (and_28_out, OPCD[0], OPCD[1], OPCD[2]);
  // Pins of 7 and 8 bits meet at {DADO, PC, LD, STR, BRG, IMM}

  // Notes on the sheet:
  //   contents of rom_1 (hex, n*v repeats v):
  //   0,4,c,d,a,0,4,c
endmodule
