// Digital circuit IMMEXT.dig as structural Verilog
module IMMEXT (
  input  [24:0] E,
  input  [1:0] TPIMM,
  output [31:0] S
);

  Multiplexer #(.Selector_Bits(2), .Bits(32)) multiplexer_1 (
    .sel(TPIMM), .in_0({{13{E[24]}}, E[12:5], E[13], E[23:14]}),
    .in_1({{21{E[24]}}, E[0], E[23:18], E[4:1]}), .in_2({{21{E[24]}}, E[23:18], E[4:0]}),
    .in_3({{21{E[24]}}, E[23:13]}), .out(S));
endmodule
