// Digital circuit ULA.dig as structural Verilog
module ULA (
  input  [31:0] RS1,
  input  [31:0] RS2,
  input  [2:0] E,
  output ERRO,
  output [31:0] S
);

  wire add_1_cout, sub_1_of;
  wire [31:0] add_1_s, and_1_s, or_1_s, sll_1_s, slt_1_s, sub_1_s, xor_1_s;

  ADD add_1 (.RS1(RS1), .RS2(RS2), .Cout(add_1_cout), .S(add_1_s));
  SUB sub_1 (.RS1(RS1), .RS2(RS2), .OF(sub_1_of), .S(sub_1_s));
  AND and_1 (.RS1(RS1), .RS2(RS2), .S(and_1_s));
  SLL sll_1 (.RS1(RS1), .RS2(RS2), .S(sll_1_s));
  OR or_1 (.RS1(RS1), .RS2(RS2), .S(or_1_s));
  XOR xor_1 (.RS1(RS1), .RS2(RS2), .S(xor_1_s));
  SLT slt_1 (.RS1(RS1), .RS2(RS2), .S(slt_1_s));
  or or_2 (ERRO, add_1_cout, sub_1_of);
  Multiplexer #(.Selector_Bits(3), .Bits(32)) multiplexer_1 (
    .sel(E), .in_0({32{1'b0}}), .in_1(add_1_s), .in_2(sub_1_s), .in_3(and_1_s), .in_4(sll_1_s),
    .in_5(or_1_s), .in_6(xor_1_s), .in_7(slt_1_s), .out(S));
endmodule
